# Fritzing sketch arduino_circuit_design (saved by Fritzing 1.0.4)
breadboards: 1

parts:
  R1 = Photocell (LDR) [power=0.25W dark_resistance_@0.01lx=300kΩ light_resistance_@100lx=400Ω luminance=10lx package=THT]
  R2 = Resistor [tolerance=±0.25% power=0.25W resistance=120k package=THT]
  R3 = Resistor [tolerance=±0.25% power=0.25W resistance=120k package=THT]
  LED1 = LED - 5mm [color="Green (555nm)" current=0.030A package="5 mm [THT]"]
  R4 = Resistor [tolerance=±5% power=0.25W resistance=10k package=THT]
  R5 = Resistor [tolerance=±5% power=0.25W resistance=10k package=THT]
  R6 = Resistor [tolerance=±5% power=0.25W resistance=1k package=THT]
  Bauteil1 = Arduino Uno (Rev3)
  S1 = Pushbutton [package=THT]
  R7 = 12mm Trimmer Potentiometer (Large) [maximum_resistance=10kΩ knob_status=50% power=0.5W package=THT]

nets:
  N1: R1.pin_0, Bauteil1.5V, S1.leg1, R7.leg1
  N2: R1.pin_1, R2.Pin_0, Bauteil1.A2
  N3: R2.Pin_1, R3.Pin_1
  N4: R3.Pin_0, LED1.cathode, R5.Pin_1, R6.Pin_1, Bauteil1.GND
  N5: LED1.anode, R4.Pin_1
  N6: R4.Pin_0, Bauteil1.D10_PWM/SS
  N7: R5.Pin_0, Bauteil1.A0, R7.wiper
  N8: R6.Pin_0, Bauteil1.A1, S1.leg0

notes:
  Rotary Potentiometer on Water boiler bottom
  Water boiler switch
  Photocell inside water boiler
